# Fritzing sketch Bolt lightMINI (Breadboard, Schematics, PCB) (saved by Fritzing 0.9.3b)
circuit board: 7.34226cm x 4.8258cm

parts:
  Q1 = npn-Powertransistor [package="TO220 [THT]"]
  VCC = Battery block 9V
  STS = LED - 3mm [color="Red (633nm)" package="3 mm [THT]"]
  AJ1 = Audio Jack Breakout
  R2 = Resistor [tolerance=±5% resistance=680 package=THT]
  LED_OUT = LED - 3mm [color="Red (633nm)" package="3 mm [THT]"]

nets:
  N1: Q1.base, AJ1.RING, AJ1.TIP
  N2: Q1.collector, AJ1.GND
  N3: Q1.emitter, LED_OUT.cathode
  N4: VCC.-, R2.Pin_0, LED_OUT.anode
  N5: VCC.+, STS.cathode
  N6: STS.anode, R2.Pin_1

notes:
  board 1.0
  B C E
  - +
